// Logisim project UNSC.circ as structural Verilog: 7 circuits, main circuit main
module main (
  input  in_1
);

  wire clock_1_out, control_1_p2, register_2_p2;
  wire [15:0] adder_1_out, multiplexer_1_out, multiplexer_2_out, register_1_q;

  Clock clock_1 (.out(clock_1_out));
  Register #(.width(16)) register_1 (
    .D(multiplexer_2_out), .Q(register_1_q), .clk(clock_1_out), .clr(in_1));  // open: en
  // Register #(.width(16)) register_2: pin names not known; wires that end beside it: register_1_q, register_2_p2
  Adder #(.width(16)) adder_1 (.a(16'h1), .b(register_1_q), .out(adder_1_out));  // open: cin, cout
  // control control_1: pin names not known; wires that end beside it: register_2_p2, control_1_p2
  // banco banco_1: pin names not known; wires that end beside it: register_2_p2, register_2_p2, register_2_p2, register_2_p2
  Multiplexer #(.width(16)) multiplexer_1 (
    .in1(adder_1_out), .out(multiplexer_1_out), .sel(control_1_p2));  // open: in0, en
  Multiplexer #(.width(16)) multiplexer_2 (.in0(multiplexer_1_out), .out(multiplexer_2_out));  // open: in1, sel, en

  // Notes on the sheet:
  //   dividir esses bits?
endmodule

module ula_16 (
  input  [15:0] in_1,
  input  in_2,
  input  [15:0] in_3,
  input  in_4,
  input  [1:0] in_5,
  output [15:0] out_6,
  output out_7,
  output out_8
);

  wire [15:0] adder_1_out, and_1_out, multiplexer_1_out, multiplexer_2_out, multiplier_1_out, not_1_out,
       not_2_out, or_1_out;

  Multiplexer #(.width(16)) multiplexer_1 (
    .in0(in_1), .in1(not_1_out), .out(multiplexer_1_out), .sel(in_2));  // open: en
  assign not_1_out = ~in_1;  // NOT_Gate not_1, 16 bits wide
  Multiplexer #(.width(16)) multiplexer_2 (
    .in0(in_3), .in1(not_2_out), .out(multiplexer_2_out), .sel(in_4));  // open: en
  assign not_2_out = ~in_3;  // NOT_Gate not_2, 16 bits wide
  assign and_1_out = multiplexer_1_out & multiplexer_2_out;  // AND_Gate and_1, 16 bits wide
  assign or_1_out = multiplexer_1_out | multiplexer_2_out;  // OR_Gate or_1, 16 bits wide
  Adder #(.width(16)) adder_1 (
    .a(multiplexer_1_out), .b(multiplexer_2_out), .out(adder_1_out), .cout(out_7));  // open: cin
  Multiplier #(.width(16)) multiplier_1 (
    .a(multiplexer_1_out), .b(multiplexer_2_out), .out(multiplier_1_out));  // open: cin, cout
  Comparator #(.width(16)) comparator_1 (.a(multiplexer_1_out), .b(multiplexer_2_out), .eq(out_8));  // open: gt, lt
  Multiplexer #(.select(2), .width(16)) multiplexer_3 (
    .in0(and_1_out), .in1(or_1_out), .in2(adder_1_out), .in3(multiplier_1_out), .out(out_6), .sel(in_5));  // open: en

  // Notes on the sheet:
  //   aqui vem os dados para serem realizados operacoes, todos os bits de uma vez, com a saida resultado e zero, 4 operacoes
endmodule

module banco (
  input  [15:0] in_1,
  input  [3:0] in_2,
  input  in_3,
  input  [3:0] in_4,
  input  in_5,
  input  [3:0] in_6,
  output [15:0] out_7,
  output [15:0] out_8
);

  wire demultiplexer_1_out0, demultiplexer_1_out1, demultiplexer_1_out2, demultiplexer_1_out3,
       demultiplexer_1_out4, demultiplexer_1_out5, demultiplexer_1_out6, demultiplexer_1_out7,
       demultiplexer_1_out8, demultiplexer_1_out9, demultiplexer_1_out10, demultiplexer_1_out11,
       demultiplexer_1_out12, demultiplexer_1_out13, demultiplexer_1_out14, demultiplexer_1_out15;
  wire [15:0] register_1_q, register_2_q, register_3_q, register_4_q, register_5_q, register_6_q,
       register_7_q, register_8_q, register_9_q, register_10_q, register_11_q, register_12_q, register_13_q,
       register_14_q, register_15_q, register_16_q;

  Demultiplexer #(.select(4)) demultiplexer_1 (
    .out0(demultiplexer_1_out0), .out1(demultiplexer_1_out1), .out2(demultiplexer_1_out2),
    .out3(demultiplexer_1_out3), .out4(demultiplexer_1_out4), .out5(demultiplexer_1_out5),
    .out6(demultiplexer_1_out6), .out7(demultiplexer_1_out7), .out8(demultiplexer_1_out8),
    .out9(demultiplexer_1_out9), .out10(demultiplexer_1_out10), .out11(demultiplexer_1_out11),
    .out12(demultiplexer_1_out12), .out13(demultiplexer_1_out13), .out14(demultiplexer_1_out14),
    .out15(demultiplexer_1_out15), .in(in_3), .sel(in_4));  // open: en
  Register #(.width(16)) register_1 (.D(in_1), .en(demultiplexer_1_out0), .Q(register_1_q), .clk(in_5));  // open: clr
  Register #(.width(16)) register_2 (.D(in_1), .en(demultiplexer_1_out1), .Q(register_2_q), .clk(in_5));  // open: clr
  Register #(.width(16)) register_3 (.D(in_1), .en(demultiplexer_1_out2), .Q(register_3_q), .clk(in_5));  // open: clr
  Register #(.width(16)) register_4 (.D(in_1), .en(demultiplexer_1_out3), .Q(register_4_q), .clk(in_5));  // open: clr
  Register #(.width(16)) register_5 (.D(in_1), .en(demultiplexer_1_out4), .Q(register_5_q), .clk(in_5));  // open: clr
  Register #(.width(16)) register_6 (.D(in_1), .en(demultiplexer_1_out5), .Q(register_6_q), .clk(in_5));  // open: clr
  Register #(.width(16)) register_7 (.D(in_1), .en(demultiplexer_1_out6), .Q(register_7_q), .clk(in_5));  // open: clr
  Register #(.width(16)) register_8 (.D(in_1), .en(demultiplexer_1_out7), .Q(register_8_q), .clk(in_5));  // open: clr
  Register #(.width(16)) register_9 (.D(in_1), .en(demultiplexer_1_out8), .Q(register_9_q));  // open: clk, clr
  Register #(.width(16)) register_10 (.D(in_1), .en(demultiplexer_1_out9), .Q(register_10_q), .clk(in_5));  // open: clr
  Register #(.width(16)) register_11 (
    .D(in_1), .en(demultiplexer_1_out10), .Q(register_11_q), .clk(in_5));  // open: clr
  Register #(.width(16)) register_12 (
    .D(in_1), .en(demultiplexer_1_out11), .Q(register_12_q), .clk(in_5));  // open: clr
  Register #(.width(16)) register_13 (
    .D(in_1), .en(demultiplexer_1_out12), .Q(register_13_q), .clk(in_5));  // open: clr
  Register #(.width(16)) register_14 (
    .D(in_1), .en(demultiplexer_1_out13), .Q(register_14_q), .clk(in_5));  // open: clr
  Register #(.width(16)) register_15 (
    .D(in_1), .en(demultiplexer_1_out14), .Q(register_15_q), .clk(in_5));  // open: clr
  Register #(.width(16)) register_16 (
    .D(in_1), .en(demultiplexer_1_out15), .Q(register_16_q), .clk(in_5));  // open: clr
  Multiplexer #(.select(4), .width(16)) multiplexer_1 (
    .in0(register_1_q), .in1(register_2_q), .in2(register_3_q), .in3(register_4_q), .in4(register_5_q),
    .in5(register_6_q), .in6(register_7_q), .in7(register_8_q), .in8(register_9_q), .in9(register_10_q),
    .in10(register_11_q), .in11(register_12_q), .in12(register_13_q), .in13(register_14_q),
    .in14(register_15_q), .in15(register_16_q), .out(out_7), .sel(in_2));  // open: en
  Multiplexer #(.select(4), .width(16)) multiplexer_2 (
    .in0(register_16_q), .in1(register_15_q), .in2(register_13_q), .in3(register_14_q), .in4(register_12_q),
    .in5(register_11_q), .in6(register_10_q), .in7(register_9_q), .in8(register_8_q), .in9(register_7_q),
    .in10(register_6_q), .in11(register_5_q), .in12(register_4_q), .in13(register_3_q), .in14(register_2_q),
    .in15(register_1_q), .out(out_8), .sel(in_6));  // open: en

  // Notes on the sheet:
  //   banco de registradores, qual eu vou acessar, quais sao os dados presentes nos referenciados pela instrucao, e se eu vou escrever neles
endmodule

module pc (
  input  [15:0] in_1,
  input  in_2,
  output [15:0] out_3,
  output [1:0] out_4
);

  wire counter_1_carry;

  Counter #(.width(2), .max('h3)) counter_1 (
    .D(2'b11), .count(1'b1), .Q(out_4), .carry(counter_1_carry), .clk(in_2), .clr(counter_1_carry));  // open: load
  Register #(.width(16)) register_1 (.D(in_1), .Q(out_3), .clk(counter_1_carry));  // open: en, clr
endmodule

module fetch (
  input  [15:0] in_1,
  input  in_2,
  input  in_3,
  output [15:0] out_4
);

  wire [1:0] adder_1_out, register_2_q;
  wire [15:0] multiplexer_1_out, register_1_q;

  Adder #(.width(2)) adder_1 (.a(register_2_q), .b(2'b01), .out(adder_1_out));  // open: cin, cout
  Register #(.width(16)) register_1 (.D(in_1), .Q(register_1_q), .clk(in_3), .clr(in_2));  // open: en
  Register #(.width(2)) register_2 (.D(adder_1_out), .Q(register_2_q), .clk(in_3), .clr(in_2));  // open: en
  Register #(.width(16)) register_3 (.D(multiplexer_1_out), .Q(out_4), .clk(in_3), .clr(in_2));  // open: en
  Multiplexer #(.width(16)) multiplexer_1 (.in0(in_1), .in1(register_1_q), .out(multiplexer_1_out));  // open: sel, en

  // Notes on the sheet:
  //   encontrar a instrucao e informa-la ao sistema
  //   erro na conexao para permitir a gravacao
endmodule

module control (
  input  in_1,
  input  in_2,
  input  in_3,
  input  in_4,
  input  in_5,
  input  in_6,
  output out_7,
  output out_8,
  output out_9,
  output out_10,
  output out_11,
  output out_12,
  output out_13,
  output out_14,
  output out_15,
  output out_16,
  output out_17
);

  wire and_1_out, and_2_out, and_3_out, undriven;

  // AND_Gate and_1 has open pins: out=and_1_out
  // AND_Gate and_2 has open pins: out=and_2_out
  // AND_Gate and_3 has open pins: out=and_3_out
  or or_1 (out_9, and_1_out, and_2_out, and_3_out, undriven);

  // Notes on the sheet:
  //   RD
  //   Branch
  //   MR
  //   MTR
  //   ULA0
  //   ULA1
  //   ULA2
  //   MW
  //   ULAS
  //   RW
  //   J
  //   (!4 e 6) ou (!3 e 5) ou (!3 e 4) ou (3 e !5) ou (3 e !4) ou (2 e !3) ou (1 e !3)
endmodule

module control_ula (
  input  in_1,
  input  in_2,
  input  in_3,
  output b,
  output [2:0] out_5,
  output a
);

  wire and_1_out, not_1_out, not_2_out;

  not not_1 (not_1_out, in_3);
  and and_1 (and_1_out, in_2, not_1_out);
  not not_2 (not_2_out, in_3);
  or or_1 (b, and_1_out, in_1);
  // AND_Gate and_2 has open pins: in0=in_2, in1=not_2_out, out=open

  // Notes on the sheet:
  //   corrigir logica do opcode
  //   (r v s) ^ (r v !s)
  //   inverter b: (2 e !3) ou 1 
endmodule
